# Fritzing sketch lighthouse-leds-1 (saved by Fritzing 1.0.1rc)
breadboards: 1

parts:
  Pico_H1 = Raspberry Pi Pico H
  R1 = Resistor [tolerance=±5% power=0.25W resistance=1k package=THT]
  LED1 = smd LED [color="White (6500K)" package="0805 [SMD]"]
  R2 = Resistor [tolerance=±5% power=0.25W resistance=1k package=THT]
  LED2 = smd LED [color="White (6500K)" package="0805 [SMD]"]
  LED3 = smd LED [color="White (6500K)" package="0805 [SMD]"]
  LED4 = smd LED [color="White (6500K)" package="0805 [SMD]"]
  LED5 = smd LED [color="White (6500K)" package="0805 [SMD]"]
  R3 = Resistor [tolerance=±5% power=0.25W resistance=1k package=THT]
  R4 = Resistor [tolerance=±5% power=0.25W resistance=1k package=THT]
  R6 = Resistor [tolerance=±5% power=0.25W resistance=1k package=THT]

nets:
  N1: Pico_H1.GP19, R3.Pin_1
  N2: Pico_H1.GP18, R6.Pin_1
  N3: Pico_H1.GP17, R2.Pin_1
  N4: Pico_H1.GP16, R1.Pin_1
  N5: R1.Pin_0, LED1.anode
  N6: LED1.cathode, LED2.cathode, LED3.cathode, LED4.cathode, LED5.cathode
  N7: R2.Pin_0, LED2.anode
  N8: LED3.anode, R6.Pin_0
  N9: LED4.anode, R3.Pin_0
  N10: LED5.anode, R4.Pin_0

custom parts:
  Raspberry Pi Pico H: Raspberry Pi Pico H. Based around the RP2040 microcontroller the Pico H is a low cost microcontroller device bringing Raspberry Pi quality, cost, and easy of use to the microcontroller space.
